// Logisim project decodificadorBinarioDecimal.circ as structural Verilog: 2 circuits, main circuit main
module main (
  output q0,
  output q1,
  output q2,
  output q3
);

  wire binarioparadisplay_1_a_2, binarioparadisplay_1_b_2, binarioparadisplay_1_c_2,
       binarioparadisplay_1_d_2, binarioparadisplay_1_e, binarioparadisplay_1_f, binarioparadisplay_1_g,
       clock_1_out, reset;

  Clock clock_1 (.out(clock_1_out));
  T_Flip_Flop #(.trigger("falling")) t_ff_1 (
    .clk(clock_1_out), .T(1'b1), .Q(q3), .reset(reset));  // open: Qn, preset, en
  binarioparaDisplay binarioparadisplay_1 (
    .A(q0), .B(q1), .C(q2), .D(q3), .a_2(binarioparadisplay_1_a_2), .b_2(binarioparadisplay_1_b_2),
    .c_2(binarioparadisplay_1_c_2), .d_2(binarioparadisplay_1_d_2), .e(binarioparadisplay_1_e),
    .f(binarioparadisplay_1_f), .g(binarioparadisplay_1_g));
  T_Flip_Flop #(.trigger("falling")) t_ff_2 (.clk(q3), .T(1'b1), .Q(q2), .reset(reset));  // open: Qn, preset, en
  T_Flip_Flop #(.trigger("falling")) t_ff_3 (.clk(q2), .T(1'b1), .Q(q1), .reset(reset));  // open: Qn, preset, en
  T_Flip_Flop #(.trigger("falling")) t_ff_4 (.clk(q1), .T(1'b1), .Q(q0), .reset(reset));  // open: Qn, preset, en
  _7_Segment_Display u_7_segment_display_1 (
    .g(binarioparadisplay_1_g), .f(binarioparadisplay_1_f), .a(binarioparadisplay_1_b_2),
    .b(binarioparadisplay_1_a_2), .e(binarioparadisplay_1_e), .d(binarioparadisplay_1_d_2),
    .c(binarioparadisplay_1_c_2));  // open: dp
  and and_1 (reset, q2, q0);
endmodule

module binarioparaDisplay (
  input  A,
  input  B,
  input  C,
  input  D,
  output a_2,
  output b_2,
  output c_2,
  output d_2,
  output e,
  output f,
  output g
);

  wire and_1_out, and_2_out, and_3_out, and_4_out, and_5_out, and_6_out, and_7_out, and_8_out, and_9_out,
       and_10_out, and_11_out, and_12_out, and_13_out, and_14_out, and_15_out, and_16_out, not_1_out,
       not_2_out, not_3_out, not_4_out, not_5_out, not_6_out, not_7_out, not_8_out, not_9_out, not_10_out,
       not_11_out, not_12_out, not_13_out, not_14_out, not_15_out, not_16_out, not_17_out, not_18_out,
       not_19_out, not_20_out, not_21_out, not_22_out, not_23_out;

  not not_1 (not_1_out, B);
  not not_2 (not_2_out, C);
  and and_1 (and_1_out, not_2_out, not_3_out);
  not not_3 (not_3_out, D);
  and and_2 (and_2_out, C, D);
  not not_4 (not_4_out, B);
  and and_3 (and_3_out, not_4_out, not_5_out);
  not not_5 (not_5_out, D);
  and and_4 (and_4_out, B, D);
  not not_6 (not_6_out, C);
  not not_7 (not_7_out, B);
  and and_5 (and_5_out, not_7_out, not_8_out);
  not not_8 (not_8_out, D);
  not not_9 (not_9_out, B);
  and and_6 (and_6_out, not_9_out, C);
  and and_7 (and_7_out, C, not_10_out);
  not not_10 (not_10_out, D);
  and and_8 (and_8_out, B, not_11_out, D);
  not not_11 (not_11_out, C);
  not not_12 (not_12_out, B);
  not not_13 (not_13_out, C);
  and and_9 (and_9_out, not_12_out, not_13_out, not_14_out);
  not not_14 (not_14_out, D);
  not not_15 (not_15_out, A);
  and and_10 (and_10_out, not_15_out, C, not_16_out);
  not not_16 (not_16_out, D);
  not not_17 (not_17_out, C);
  and and_11 (and_11_out, not_17_out, not_18_out);
  not not_18 (not_18_out, D);
  and and_12 (and_12_out, B, not_19_out);
  not not_19 (not_19_out, C);
  and and_13 (and_13_out, B, not_20_out);
  not not_20 (not_20_out, D);
  not not_21 (not_21_out, B);
  and and_14 (and_14_out, not_21_out, C);
  and and_15 (and_15_out, B, not_22_out);
  not not_22 (not_22_out, C);
  and and_16 (and_16_out, B, not_23_out);
  not not_23 (not_23_out, D);
  or or_1 (a_2, not_1_out, and_1_out, and_2_out, A);
  or or_2 (b_2, and_3_out, C, and_4_out, A);
  or or_3 (c_2, not_6_out, D, B, A);
  or or_4 (d_2, and_5_out, and_6_out, and_7_out, and_8_out, A);
  or or_5 (e, and_9_out, and_10_out);
  or or_6 (f, and_11_out, and_12_out, and_13_out, A);
  or or_7 (g, and_14_out, and_15_out, and_16_out, A);
endmodule
